# Fritzing sketch capTester (saved by Fritzing 0.9.3b)
breadboards: 1

parts:
  Part1 = Zeta LCD keypad shield for Arduino
  C1 = Capacitor Polarized [package=panasonic_e]

nets:
  N1: Part1.A1, C1.-
  N2: Part1.A2, C1.+

custom parts:
  Zeta LCD keypad shield for Arduino: The LCD shield for Arduino
