# Fritzing sketch resTester (saved by Fritzing 0.9.3b)
breadboards: 1

parts:
  Part1 = Zeta LCD keypad shield for Arduino
  R2 = Resistor [tolerance=±5% resistance=15k package=THT]
  R3 = Resistor [tolerance=±5% resistance=220 package=THT]

nets:
  N1: Part1.GND, R2.Pin_1
  N2: Part1.A2, R2.Pin_0, R3.Pin_0
  N3: Part1.+5V, R3.Pin_1

custom parts:
  Zeta LCD keypad shield for Arduino: The LCD shield for Arduino
