# Fritzing sketch volTester (saved by Fritzing 0.9.3b)
breadboards: 1

parts:
  Part1 = Zeta LCD keypad shield for Arduino
  R1 = Resistor [tolerance=±5% resistance=10k package=THT]
  R2 = Resistor [tolerance=±5% resistance=5k package=THT]

nets:
  N1: Part1.GND, R2.Pin_1
  N2: Part1.A2, R1.Pin_1

custom parts:
  Zeta LCD keypad shield for Arduino: The LCD shield for Arduino
